# Fritzing sketch GinoSeridon_TemperatureHumiditySensorV1 (saved by Fritzing 0.9.3b)
circuit board: 2.28108cm x 4.12161cm
breadboards: 1

parts:
  Part1 = Adafruit Si7021 Temp Humidity [part_number="Adafruit #3251"]
  Raspberry_Pi_1 = Raspberry Pi 3 [part_number=RPI-3-V1.2]

nets:
  N1: Part1.SDA, Raspberry_Pi_1.GPIO2
  N2: Part1.SCL, Raspberry_Pi_1.GPIO3
  GND: Part1.GND, Raspberry_Pi_1.GND
  3V3: Part1.VIN, Raspberry_Pi_1.3v3, Raspberry_Pi_1.3V3

notes:
  Gino Seridon

custom parts:
  Adafruit Si7021 Temp Humidity: It's summer and you're sweating and your hair's all frizzy and all you really want to know is why the weatherman said this morning that today's relative humidity would max out at a perfectly reasonable 42% when it feels more like 77%. Enter the Si7021 Temperature + Humidity Sensor - the best way to prove the weatherman wrong! This lovely sensor for Silicon labs has ± 3% relative humidity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
