# Fritzing sketch GinoSeridon_TemperatureHumiditySensorWithoutPiV1 (saved by Fritzing 0.9.3b)
circuit board: 2.33492cm x 4.0519cm
breadboards: 1

parts:
  J2 = female pin header, 5 pins [form="♀ (female)"]
  J1 = double row female pin header, 6 pins [form="♀ (female)"]

nets:
  N1: J2.pin1, J1.pin1
  N2: J2.pin3, J1.pin4
  N3: J2.pin4, J1.pin3
  N4: J2.pin5, J1.pin2

notes:
  Gino Seridon
  3Vin
  GND
  SCL
  SDA
  RPi
  Si7021
